// Logisim project CPU Proto1.circ as structural Verilog
module MEM_1 (
  input  s,
  input  E,
  output Q
);

  wire nand_1_out, nand_2_out, nand_4_out;

  nand nand_1 (nand_1_out, s, E);
  nand nand_2 (nand_2_out, nand_1_out, E);
  nand nand_3 (Q, nand_1_out, nand_4_out);
  nand nand_4 (nand_4_out, Q, nand_2_out);
endmodule

module MEM_8 (
  input  [7:0] \input ,
  input  set,
  output [7:0] out_3
);

  MEM_1 mem_1_1 (.s(\input [0]), .E(set), .Q(out_3[0]));
  MEM_1 mem_1_2 (.s(\input [1]), .E(set), .Q(out_3[1]));
  MEM_1 mem_1_3 (.s(\input [2]), .E(set), .Q(out_3[2]));
  MEM_1 mem_1_4 (.s(\input [3]), .E(set), .Q(out_3[3]));
  MEM_1 mem_1_5 (.s(\input [4]), .E(set), .Q(out_3[4]));
  MEM_1 mem_1_6 (.s(\input [5]), .E(set), .Q(out_3[5]));
  MEM_1 mem_1_7 (.s(\input [6]), .E(set), .Q(out_3[6]));
  MEM_1 mem_1_8 (.s(\input [7]), .E(set), .Q(out_3[7]));
endmodule

module CPU_ENABLE (
  input  [7:0] \input ,
  input  enable,
  output [7:0] out_3
);

  and and_1 (out_3[0], \input [0], enable);
  and and_2 (out_3[1], \input [1], enable);
  and and_3 (out_3[2], \input [2], enable);
  and and_4 (out_3[3], \input [3], enable);
  and and_5 (out_3[4], \input [4], enable);
  and and_6 (out_3[5], \input [5], enable);
  and and_7 (out_3[6], \input [6], enable);
  and and_8 (out_3[7], \input [7], enable);
endmodule

module DECODER_3x8 (
  input  MSB,
  input  middle,
  input  LSB,
  output [7:0] out_4
);

  wire not_1_out, not_2_out, not_3_out;

  not not_1 (not_1_out, MSB);
  not not_2 (not_2_out, middle);
  not not_3 (not_3_out, LSB);
  and _000 (out_4[0], not_1_out, not_2_out, not_3_out);
  and _001 (out_4[1], not_1_out, not_2_out, LSB);
  and _010 (out_4[2], not_1_out, middle, not_3_out);
  and _011 (out_4[3], not_1_out, middle, LSB);
  and _100 (out_4[4], MSB, not_2_out, not_3_out);
  and _101 (out_4[5], MSB, not_2_out, LSB);
  and _110 (out_4[6], MSB, middle, not_3_out);
  and _111 (out_4[7], MSB, middle, LSB);
endmodule

module DECODER_4x16 (
  input  [3:0] \input ,
  output LSB,
  output out_3,
  output out_4,
  output out_5,
  output out_6,
  output out_7,
  output out_8,
  output out_9,
  output out_10,
  output out_11,
  output out_12,
  output out_13,
  output out_14,
  output out_15,
  output out_16,
  output MSB
);

  wire not_1_out, not_2_out, not_3_out, not_4_out;

  not not_1 (not_1_out, \input [0]);
  not not_2 (not_2_out, \input [1]);
  not not_3 (not_3_out, \input [2]);
  not not_4 (not_4_out, \input [3]);
  and _0000 (LSB, not_4_out, not_3_out, not_2_out, not_1_out);
  and _0001 (out_3, not_4_out, not_3_out, not_2_out, \input [0]);
  and _0010 (out_4, not_4_out, not_3_out, \input [1], not_1_out);
  and _0011 (out_5, not_4_out, not_3_out, \input [1], \input [0]);
  and _0100 (out_6, not_4_out, \input [2], not_2_out, not_1_out);
  and _0101 (out_7, not_4_out, \input [2], not_2_out, \input [0]);
  and _0110 (out_8, not_4_out, \input [2], \input [1], not_1_out);
  and _0111 (out_9, not_4_out, \input [2], \input [1], \input [0]);
  and _1000 (out_10, \input [3], not_3_out, not_2_out, not_1_out);
  and _1001 (out_11, \input [3], not_3_out, not_2_out, \input [0]);
  and _1010 (out_12, \input [3], not_3_out, \input [1], not_1_out);
  and _1011 (out_13, \input [3], not_3_out, \input [1], \input [0]);
  and _1100 (out_14, \input [3], \input [2], not_2_out, not_1_out);
  and _1101 (out_15, \input [3], \input [2], not_2_out, \input [0]);
  and _1110 (out_16, \input [3], \input [2], \input [1], not_1_out);
  and _1111 (MSB, \input [3], \input [2], \input [1], \input [0]);
endmodule

module REGISTER (
  input  [7:0] input__write__data,
  input  set_bit,
  input  enable,
  output [7:0] current_register_data,
  output [7:0] output__read__bits
);

  wire [7:0] cpu_enable_1_out_3;

  MEM_8 mem_8_1 (.\input (input__write__data), .out_3(current_register_data), .set(set_bit));
  assign output__read__bits = enable ? cpu_enable_1_out_3 : 8'bz;  // Controlled_Buffer controlled_buffer_1
  CPU_ENABLE cpu_enable_1 (.\input (current_register_data), .out_3(cpu_enable_1_out_3), .enable(enable));

  // Notes on the sheet:
  //   designed for RAM memory matrix 
  //   built in buffer
endmodule

module BYTE_REGISTER (
  input  row__n,
  input  [7:0] \input ,
  input  col__m,
  input  reset,
  input  set__write_mode,
  input  enable__read_mode,
  output [7:0] contents,
  output [7:0] \output 
);

  wire Active, read_out, reset_out, write_out;
  wire [7:0] register_1_output__read__bits;

  and entry (Active, row__n, col__m);
  and write (write_out, Active, set__write_mode);
  and read (read_out, enable__read_mode, Active);
  or u_reset (reset_out, reset, write_out);
  REGISTER register_1 (
    .input__write__data(\input ), .enable(read_out), .current_register_data(contents),
    .output__read__bits(register_1_output__read__bits), .set_bit(reset_out));
  assign \output  = read_out ? register_1_output__read__bits : 8'bz;  // Controlled_Buffer controlled_buffer_1
endmodule

module Active_Low_SR_Latch (
  input  s,
  input  r,
  output Q,
  output NQ
);

  nand nand_1 (Q, s, NQ);
  nand nand_2 (NQ, Q, r);
endmodule

module _2_x_4_Decoder (
  input  A,
  input  B
);

  wire _00_out, _01_out, _10_out, _11_out, not_1_out, not_2_out;

  not not_1 (not_1_out, A);
  not not_2 (not_2_out, B);
  and _00 (_00_out, not_1_out, not_2_out);
  and _01 (_01_out, not_1_out, B);
  and _10 (_10_out, A, not_2_out);
  and _11 (_11_out, A, B);

  // Notes on the sheet:
  //   !A
  //   !B
endmodule

module Active_High_SR_Latch_w__Enable (
  input  s,
  input  E,
  output Q,
  output NQ
);

  wire nand_1_out, nand_2_out, not_1_out;

  not not_1 (not_1_out, s);
  nand nand_1 (nand_1_out, s, E);
  nand nand_2 (nand_2_out, E, not_1_out);
  nand nand_3 (Q, nand_1_out, NQ);
  nand nand_4 (NQ, Q, nand_2_out);
endmodule

module register_model (
  input  [7:0] i,
  input  set,
  input  enable,
  output [7:0] o
);

  wire [7:0] mem_8_1_out_3;

  MEM_8 mem_8_1 (.\input (i), .out_3(mem_8_1_out_3), .set(set));
  CPU_ENABLE cpu_enable_1 (.\input (mem_8_1_out_3), .out_3(o), .enable(enable));

  // Notes on the sheet:
  //   simple version w/ no buffer or control
endmodule
